// Logisim project cpu.circ as structural Verilog: 4 circuits, main circuit CPU
module CPU (
);

  wire clk, comparator_1_eq, I, reset, undriven, undriven_2;
  wire [2:0] adder_2_out, AluOp, DestReg, Mux_equals4, RdQ, SrcReg1, state_reg_q;
  wire [15:0] adder_1_out, bit_extender_1_out, InsMem_data, IR_q, MuxOut, PC_q, RA_q, RbQ, registerfile_1_a,
       registerfile_1_b, RwQ, RZ_q, undriven_3;

  Clock u_clk (.out(clk));
  Button u_reset (.out(reset));
  Register #(.width(16)) PC (.D(adder_1_out), .Q(PC_q));  // open: en, clk, clr
  Adder #(.width(16)) adder_1 (.a(PC_q), .b(16'h1), .out(adder_1_out));  // open: cin, cout
  ROM #(.addrWidth(16), .dataWidth(16)) InsMem (.addr(PC_q), .data(InsMem_data));
  RegisterFile registerfile_1 (
    .Addr_A(DestReg), .Addr_B(SrcReg1), .Addr_C(RdQ), .reset(undriven), .C(RwQ), .A(registerfile_1_a),
    .B(registerfile_1_b));  // open: we, clk
  Register #(.width(16)) RA (.D(registerfile_1_a), .Q(RA_q));  // open: en, clk, clr
  Register #(.width(16)) RB (.D(registerfile_1_b), .Q(RbQ));  // open: en, clk, clr
  Register #(.width(16)) IR (
    .D(InsMem_data), .en(undriven_2), .Q({IR_q[15:14], AluOp, I, DestReg, SrcReg1, IR_q[3:0]}));  // open: clk, clr
  Register #(.width(3)) RD (.D(DestReg), .Q(RdQ));  // open: en, clk, clr
  ALU alu_1 (.A(RA_q), .B(MuxOut), .fun(AluOp));  // open: negative, zero, carry, overflow, C
  Register #(.width(3)) state_reg (.D(Mux_equals4), .clk(clk), .Q(state_reg_q), .clr(reset));  // open: en
  Register #(.width(16)) RZ (.D(undriven_3), .Q(RZ_q));  // open: en, clk, clr
  Adder #(.width(3)) adder_2 (.a(state_reg_q), .b(3'b001), .out(adder_2_out));  // open: cin, cout
  assign bit_extender_1_out = {{12{IR_q[3]}}, IR_q[3:0]};  // Bit_Extender bit_extender_1
  Comparator #(.width(3)) comparator_1 (.a(adder_2_out), .b(3'b101), .eq(comparator_1_eq));  // open: gt, lt
  Register #(.width(16)) RW (.D(RZ_q), .Q(RwQ));  // open: en, clk, clr
  Multiplexer #(.width(16)) multiplexer_1 (.in0(RbQ), .in1(bit_extender_1_out), .out(MuxOut), .sel(I));
  Multiplexer #(.width(3)) multiplexer_2 (.in0(adder_2_out), .in1(3'b000), .out(Mux_equals4), .sel(comparator_1_eq));

  // Notes on the sheet:
  //   contents of InsMem (hex, n*v repeats v):
  //   400 e84 1394 1e51 2534 2cd4 33d4 3f51 4380
endmodule

module ALU (
  input  [2:0] fun,
  input  [15:0] A,
  input  [15:0] B,
  output [15:0] C,
  output negative,
  output zero,
  output carry,
  output overflow
);

  wire xnor_1_out, xor_1_out;
  wire [15:0] adder_1_out, and_1_out, multiplexer_1_out, nor_1_out, not_1_out, or_1_out, shifter_1_out,
       shifter_2_out, shifter_3_out;

  assign not_1_out = ~B;  // NOT_Gate not_1, 16 bits wide
  assign and_1_out = A & B;  // AND_Gate and_1, 16 bits wide
  assign or_1_out = A | B;  // OR_Gate or_1, 16 bits wide
  assign nor_1_out = ~(A | B);  // NOR_Gate nor_1, 16 bits wide
  Multiplexer #(.width(16)) multiplexer_1 (.in0(B), .in1(not_1_out), .out(multiplexer_1_out), .sel(fun[0]));
  Shifter #(.width(16)) shifter_1 (.in(A), .\dist (B[3:0]), .out(shifter_1_out));
  Adder #(.width(16)) adder_1 (.a(A), .b(multiplexer_1_out), .out(adder_1_out), .cin(fun[0]), .cout(carry));
  Multiplexer #(.select(3), .width(16)) multiplexer_2 (
    .in0(adder_1_out), .in1(adder_1_out), .in2(and_1_out), .in3(or_1_out), .in4(nor_1_out),
    .in5(shifter_1_out), .in6(shifter_2_out), .in7(shifter_3_out), .out(C), .sel(fun));
  Shifter #(.shift("lr"), .width(16)) shifter_2 (.in(A), .\dist (B[3:0]), .out(shifter_2_out));
  Shifter #(.shift("ar"), .width(16)) shifter_3 (.in(A), .\dist (B[3:0]), .out(shifter_3_out));
  Comparator #(.width(16)) comparator_1 (.a(C), .b({16{1'b0}}), .eq(zero));  // open: gt, lt
  xnor xnor_1 (xnor_1_out, A[15], multiplexer_1_out[15]);
  xor xor_1 (xor_1_out, adder_1_out[15], A[15]);
  and and_2 (overflow, xnor_1_out, xor_1_out);

  assign negative = C[15];
endmodule

module RegisterFile (
  input  [2:0] Addr_A,
  input  [2:0] Addr_B,
  input  [2:0] Addr_C,
  input  we,
  input  clk,
  input  reset,
  input  [15:0] C,
  output [15:0] A,
  output [15:0] B
);

  wire and_1_out, and_2_out, and_3_out, and_4_out, and_5_out, and_6_out, and_7_out, and_8_out,
       decoder_1_out0, decoder_1_out1, decoder_1_out2, decoder_1_out3, decoder_1_out4, decoder_1_out5,
       decoder_1_out6, decoder_1_out7;
  wire [15:0] R0_q, R1_q, R2_q, R3_q, R4_q, R5_q, R6_q, R7_q;

  Register #(.width(16)) R0 (.D(C), .en(and_1_out), .clk(clk), .Q(R0_q), .clr(reset));
  Register #(.width(16)) R1 (.D(C), .en(and_2_out), .clk(clk), .Q(R1_q), .clr(reset));
  Register #(.width(16)) R2 (.D(C), .en(and_3_out), .clk(clk), .Q(R2_q), .clr(reset));
  Register #(.width(16)) R3 (.D(C), .en(and_4_out), .clk(clk), .Q(R3_q), .clr(reset));
  Register #(.width(16)) R4 (.D(C), .en(and_5_out), .clk(clk), .Q(R4_q), .clr(reset));
  Register #(.width(16)) R5 (.D(C), .en(and_6_out), .clk(clk), .Q(R5_q), .clr(reset));
  Register #(.width(16)) R6 (.D(C), .en(and_7_out), .clk(clk), .Q(R6_q), .clr(reset));
  Register #(.width(16)) R7 (.D(C), .en(and_8_out), .clk(clk), .Q(R7_q), .clr(reset));
  Multiplexer #(.select(3), .width(16)) multiplexer_1 (
    .in0(R0_q), .in1(R1_q), .in2(R2_q), .in3(R3_q), .in4(R4_q), .in5(R5_q), .in6(R6_q), .in7(R7_q), .out(A),
    .sel(Addr_A));
  Decoder #(.enable("false"), .select(3)) decoder_1 (
    .out0(decoder_1_out0), .out1(decoder_1_out1), .out2(decoder_1_out2), .out3(decoder_1_out3),
    .out4(decoder_1_out4), .out5(decoder_1_out5), .out6(decoder_1_out6), .out7(decoder_1_out7), .sel(Addr_C));
  Multiplexer #(.select(3), .width(16)) multiplexer_2 (
    .in0(R0_q), .in1(R1_q), .in2(R2_q), .in3(R3_q), .in4(R4_q), .in5(R5_q), .in6(R6_q), .in7(R7_q), .out(B),
    .sel(Addr_B));
  and and_1 (and_1_out, we, decoder_1_out0);
  and and_2 (and_2_out, we, decoder_1_out1);
  and and_3 (and_3_out, we, decoder_1_out2);
  and and_4 (and_4_out, we, decoder_1_out3);
  and and_5 (and_5_out, we, decoder_1_out4);
  and and_6 (and_6_out, we, decoder_1_out5);
  and and_7 (and_7_out, we, decoder_1_out6);
  and and_8 (and_8_out, we, decoder_1_out7);
endmodule

module RegisterFileTester (
  output halt,
  output [15:0] A,
  output [15:0] B,
  output clk
);

  wire undriven;
  wire [2:0] Addr_A_data, Addr_B_data, Addr_C_data;
  wire [3:0] adder_1_out, addr_q;
  wire [15:0] C_data;

  Clock clock_1 (.out(clk));
  ROM #(.addrWidth(4), .dataWidth(3)) Addr_A (.addr(addr_q), .data(Addr_A_data));
  ROM #(.addrWidth(4), .dataWidth(3)) Addr_B (.addr(addr_q), .data(Addr_B_data));
  ROM #(.addrWidth(4), .dataWidth(3)) Addr_C (.addr(addr_q), .data(Addr_C_data));
  ROM #(.addrWidth(4), .dataWidth(1)) we (.addr(addr_q));  // open: data
  ROM #(.addrWidth(4), .dataWidth(16)) C (.addr(addr_q), .data(C_data));
  Adder #(.width(4)) adder_1 (.a(addr_q), .b(4'b0001), .out(adder_1_out), .cin(1'b0));  // open: cout
  Register #(.width(4)) addr (.D(adder_1_out), .en(1'b1), .clk(clk), .Q(addr_q), .clr(1'b0));
  Comparator #(.width(4)) comparator_1 (.a(addr_q), .b(4'b1111), .eq(halt));  // open: gt, lt
  RegisterFile registerfile_1 (
    .Addr_A(Addr_A_data), .Addr_B(Addr_B_data), .Addr_C(Addr_C_data), .we(undriven), .clk(clk), .reset(1'b0),
    .C(C_data), .A(A), .B(B));

  // Notes on the sheet:
  //   contents of Addr_A (hex, n*v repeats v):
  //   5 2 7 3 2 0 2 6 2 4 1 3 5 5 2 6
  //   contents of Addr_B (hex, n*v repeats v):
  //   4 4 6 0 2 3 5 5 5 0 0 4 5 3 7 5
  //   contents of Addr_C (hex, n*v repeats v):
  //   0 5 0 5 5 7 2 3 6 4 0 4 7 7 4 6
  //   contents of we (hex, n*v repeats v):
  //   0 0 0 1 0 0 1 0 0 0 1 1 0 0 1 1
  //   contents of C (hex, n*v repeats v):
  //   1 4 c f 0 5 9 7 c b 9 f b 9 1 e
endmodule
